# Fritzing sketch Switcher (saved by Fritzing 0.9.2b)
breadboards: 1

parts:
  R5 = Resistor [tolerance=±5% resistance=1k package=THT]
  U1 = TCMT1103-OPTO [package=ssop-4]
  Q1 = Basic FET N-Channel [package="TO220 [THT]"]
  Q2 = Basic FET P-Channel [package="TO220 [THT]"]
  Q3 = Basic FET P-Channel [package="TO220 [THT]"]
  R6 = Resistor [tolerance=±5% resistance=2k package=THT]
  R7 = Resistor [tolerance=±5% resistance=500k package=THT]
  R8 = Resistor [tolerance=±5% resistance=500k package=THT]

nets:
  5V in: R5.Pin_0
  N1: R5.Pin_1, U1.A
  GND: U1.K, U1.E, Q1.source, R8.Pin_1
  N2: U1.C, Q1.gate, R6.Pin_0
  N3: Q1.drain, Q2.gate, R7.Pin_1
  600V: Q2.drain, Q3.drain, R7.Pin_0
  N4: Q2.source, Q3.gate, R8.Pin_0
  600V out: Q3.source
  12V: R6.Pin_1
