# Fritzing sketch Switcher2 (saved by Fritzing 0.9.2b)
breadboards: 1

parts:
  U1 = SO16 [chip_label=ADuM5230 package=SO]
  Q1 = Basic FET N-Channel [part_number=STx21N90K5 package="TO220 [THT]"]
  C2 = Tantalum Capacitor [capacitance="1 μF" voltage=20V part_number=T491B475K020AT package="B 3528 [SMD, tantalum]"]
  R1 = Resistor [tolerance=±5% resistance=100 package="2010 [SMD]"]
  R2 = Resistor [tolerance=±5% resistance=100 package="2010 [SMD]"]
  C3 = Tantalum Capacitor [capacitance="1 μF" voltage=10V part_number=F931A156MBA package="B 3528 [SMD, tantalum]"]
  C4 = Tantalum Capacitor [voltage=10V part_number=F931A156MBA capacitance="1 μF" package="B 3528 [SMD, tantalum]"]
  J1 = female pin header, 3 pins [form="♀ (female)"]
  Q7 = MOSFET-NCHANNEL [part_number=SSM3K324R,LF package=sot23-3]
  Q5 = MOSFET-PCHANNEL [part_number=" ZXMP2120FFTA" package=sot23-3]

nets:
  GND: U1.1, U1.8, C3.-, C4.-, J1.pin3
  5V: U1.2, U1.7, C3.+, C4.+, J1.pin2
  N1: U1.5, J1.pin1
  Vout: U1.14, Q1.source, C2.-, Q7.S
  Viso: U1.15, C2.+, Q5.D
  N2: U1.16, R2.Pin_0
  N3: Q1.gate, R1.Pin_1
  600V: Q1.drain
  N4: R1.Pin_0, Q7.D, Q5.S
  N5: R2.Pin_1, Q7.G, Q5.G
